// Logisim project cpu.circ as structural Verilog: 1 circuit, main circuit cpu
module cpu (
  input  clk,
  input  [31:0] Instruction,
  input  [31:0] MemReadData,
  output [31:0] MemAddress,
  output [31:0] ProgramCounter,
  output [31:0] ra,
  output [31:0] sp,
  output [31:0] t0,
  output [31:0] t1,
  output [31:0] t2,
  output [31:0] s0,
  output [31:0] s1,
  output [31:0] a0,
  output [3:0] MemWriteMask,
  output [31:0] MemWriteData
);

  wire ASel, branch_comp_1_breq, branch_comp_1_brlt, BSel, control_logic_1_brun, MemWEn, PCSel, RegWEn;
  wire [1:0] WBSel;
  wire [2:0] ImmSel;
  wire [3:0] ALUSel;
  wire [31:0] adder_1_out, DataToReg, IMM, multiplexer_1_out, multiplexer_2_out, multiplexer_3_out,
       multiplexer_4_out, rs1o, rs2o;

  Adder #(.width(32)) adder_1 (.a(ProgramCounter), .b(32'h4), .out(adder_1_out));  // open: cin, cout
  Multiplexer #(.width(32)) multiplexer_1 (.in0(adder_1_out), .in1(MemAddress), .out(multiplexer_1_out), .sel(PCSel));
  Register #(.width(32)) PC (.D(multiplexer_1_out), .clk(clk), .Q(ProgramCounter));  // open: en, clr
  Multiplexer #(.select(2), .width(32)) multiplexer_2 (
    .in0(DataToReg), .in1(MemAddress), .in2(adder_1_out), .in3({32{1'b1}}), .out(multiplexer_2_out),
    .sel(WBSel));
  control_logic control_logic_1 (
    .PCSel(PCSel), .RegWEn(RegWEn), .ImmSel(ImmSel), .BrUn(control_logic_1_brun), .ASel(ASel), .BSel(BSel),
    .ALUSel(ALUSel), .MemWEn(MemWEn), .WBSel(WBSel), .Instruction(Instruction), .BrEq(branch_comp_1_breq),
    .BrLt(branch_comp_1_brlt));
  regfile regfile_1 (
    .ReadIndex1(Instruction[19:15]), .ReadIndex2(Instruction[24:20]), .WriteIndex(Instruction[11:7]),
    .WriteData(multiplexer_2_out), .RegWEn(RegWEn), .clk(clk), .ra(ra), .sp(sp), .t0(t0), .t1(t1), .t2(t2),
    .s0(s0), .s1(s1), .a0(a0), .ReadData1(rs1o), .ReadData2(rs2o));
  imm_gen imm_gen_1 (.Instruction(Instruction), .ImmSel(ImmSel), .Immediate(IMM));
  Multiplexer #(.width(32)) multiplexer_3 (.in0(ProgramCounter), .in1(rs1o), .out(multiplexer_3_out), .sel(ASel));
  Multiplexer #(.width(32)) multiplexer_4 (.in0(IMM), .in1(rs2o), .out(multiplexer_4_out), .sel(BSel));
  alu alu_1 (.ALUResult(MemAddress), .A(multiplexer_3_out), .B(multiplexer_4_out), .ALUSel(ALUSel));
  branch_comp branch_comp_1 (
    .BrData1(rs1o), .BrData2(rs2o), .BrUn(control_logic_1_brun), .BrEq(branch_comp_1_breq),
    .BrLt(branch_comp_1_brlt));
  partial_store partial_store_1 (
    .Instruction(Instruction), .MemAddress(MemAddress), .DataFromReg(rs2o), .MemWEn(MemWEn),
    .MemWriteMask(MemWriteMask), .DataToMem(MemWriteData));
  partial_load partial_load_1 (
    .Instruction(Instruction), .MemAddress(MemAddress), .DataFromMem(MemReadData), .DataToReg(DataToReg));

  // Other names for the same wires on the sheet: ALUResult[31:0] = MemAddress; opcode[6:0] = Instruction[6:0];
  //   rD[4:0] = Instruction[11:7]; funct3[2:0] = Instruction[14:12]; rs1[4:0] = Instruction[19:15];
  //   rs2[4:0] = Instruction[24:20]; PC[31:0] = ProgramCounter

  // Notes on the sheet:
  //   To IMEM
  //   IMEM (do **NOT** move this)
  //   From IMEM
  //   Inputs/Outputs for testing. Do **NOT** move these.
  //   It is OK to move the PC, RegFile, ALU, MEM, Branch Comp, Imm Gen, Partial Load, Partial Store and Control Logic to wherever is most convenient for you when constructing your CPU, and to delete this text
  //   To DMEM
  //   DMEM (do **NOT** move this)
  //   From DMEM
endmodule
