// Logisim project partial-store.circ as structural Verilog: 1 circuit, main circuit partial_store
module partial_store (
  input  [31:0] Instruction,
  input  [31:0] MemAddress,
  input  [31:0] DataFromReg,
  input  MemWEn,
  output [3:0] MemWriteMask,
  output [31:0] DataToMem
);

  wire [3:0] multiplexer_1_out, shifter_1_out;
  wire [4:0] bit_extender_1_out, shifter_2_out;

  Multiplexer #(.select(2), .width(4)) multiplexer_1 (
    .in0(4'b0001), .in1(4'b0011), .in2(4'b1111), .out(multiplexer_1_out), .sel(Instruction[13:12]));  // open: in3
  Shifter #(.width(4)) shifter_1 (.in(multiplexer_1_out), .\dist (MemAddress[1:0]), .out(shifter_1_out));
  assign bit_extender_1_out = {{3{1'b0}}, MemAddress[1:0]};  // Bit_Extender bit_extender_1
  Multiplexer #(.width(4)) multiplexer_2 (.in0(4'b0000), .in1(shifter_1_out), .out(MemWriteMask), .sel(MemWEn));
  Shifter #(.width(5)) shifter_2 (.in(bit_extender_1_out), .\dist (3'b011), .out(shifter_2_out));
  Shifter #(.width(32)) shifter_3 (.in(DataFromReg), .\dist (shifter_2_out), .out(DataToMem));

  // Notes on the sheet:
  //   INPUTS to your circuit
  //   DON'T CHANGE THE LOCATIONS OF THE INPUTS AND OUTPUTS!
  //   OUTPUT from your circuit
endmodule
