// Logisim project regfile.circ as structural Verilog: 1 circuit, main circuit regfile
module regfile (
  input  [4:0] ReadIndex1,
  input  [4:0] ReadIndex2,
  input  [4:0] WriteIndex,
  input  [31:0] WriteData,
  input  RegWEn,
  input  clk,
  output [31:0] ra,
  output [31:0] sp,
  output [31:0] t0,
  output [31:0] t1,
  output [31:0] t2,
  output [31:0] s0,
  output [31:0] s1,
  output [31:0] a0,
  output [31:0] ReadData1,
  output [31:0] ReadData2
);

  wire w0, w1, w2, w3, w4, w5, w6, w7, w8, w9, w10, w11, w12, w13, w14, w15, w16, w17, w18, w19, w20, w21,
       w22, w23, w24, w25, w26, w27, w28, w29, w30, w31;
  wire [31:0] o0, o3, o4, o11, o12, o13, o14, o15, o16, o17, o18, o19, o20, o21, o22, o23, o24, o25, o26,
       o27, o28, o29, o30, o31;

  Register #(.width(32)) x0 (.D(WriteData), .en(1'b0), .clk(clk), .Q(o0), .clr(1'b1));
  Register #(.width(32)) x1 (.D(WriteData), .en(w1), .clk(clk), .Q(ra));  // open: clr
  Register #(.width(32)) x2 (.D(WriteData), .en(w2), .clk(clk), .Q(sp));  // open: clr
  Register #(.width(32)) x3 (.D(WriteData), .en(w3), .clk(clk), .Q(o3));  // open: clr
  Register #(.width(32)) x4 (.D(WriteData), .en(w4), .clk(clk), .Q(o4));  // open: clr
  Register #(.width(32)) x5 (.D(WriteData), .en(w5), .clk(clk), .Q(t0));  // open: clr
  Register #(.width(32)) x6 (.D(WriteData), .en(w6), .clk(clk), .Q(t1));  // open: clr
  Multiplexer #(.select(5), .width(32)) multiplexer_1 (
    .in0(o0), .in1(ra), .in2(sp), .in3(o3), .in4(o4), .in5(t0), .in6(t1), .in7(t2), .in8(s0), .in9(s1),
    .in10(a0), .in11(o11), .in12(o12), .in13(o13), .in14(o14), .in15(o15), .in16(o16), .in17(o17),
    .in18(o18), .in19(o19), .in20(o20), .in21(o21), .in22(o22), .in23(o23), .in24(o24), .in25(o25),
    .in26(o26), .in27(o27), .in28(o28), .in29(o29), .in30(o30), .in31(o31), .out(ReadData1), .sel(ReadIndex1));
  Multiplexer #(.select(5), .width(32)) multiplexer_2 (
    .in0(o0), .in1(ra), .in2(sp), .in3(o3), .in4(o4), .in5(t0), .in6(t1), .in7(t2), .in8(s0), .in9(s1),
    .in10(a0), .in11(o11), .in12(o12), .in13(o13), .in14(o14), .in15(o15), .in16(o16), .in17(o17),
    .in18(o18), .in19(o19), .in20(o20), .in21(o21), .in22(o22), .in23(o23), .in24(o24), .in25(o25),
    .in26(o26), .in27(o27), .in28(o28), .in29(o29), .in30(o30), .in31(o31), .out(ReadData2), .sel(ReadIndex2));
  Demultiplexer #(.select(5)) demultiplexer_1 (
    .out0(w0), .out1(w1), .out2(w2), .out3(w3), .out4(w4), .out5(w5), .out6(w6), .out7(w7), .out8(w8),
    .out9(w9), .out10(w10), .out11(w11), .out12(w12), .out13(w13), .out14(w14), .out15(w15), .out16(w16),
    .out17(w17), .out18(w18), .out19(w19), .out20(w20), .out21(w21), .out22(w22), .out23(w23), .out24(w24),
    .out25(w25), .out26(w26), .out27(w27), .out28(w28), .out29(w29), .out30(w30), .out31(w31), .in(RegWEn),
    .sel(WriteIndex));
  Register #(.width(32)) x7 (.D(WriteData), .en(w7), .clk(clk), .Q(t2));  // open: clr
  Register #(.width(32)) x8 (.D(WriteData), .en(w8), .clk(clk), .Q(s0));  // open: clr
  Register #(.width(32)) x9 (.D(WriteData), .en(w9), .clk(clk), .Q(s1));  // open: clr
  Register #(.width(32)) x10 (.D(WriteData), .en(w10), .clk(clk), .Q(a0));  // open: clr
  Register #(.width(32)) x11 (.D(WriteData), .en(w11), .clk(clk), .Q(o11));  // open: clr
  Register #(.width(32)) x12 (.D(WriteData), .en(w12), .clk(clk), .Q(o12));  // open: clr
  Register #(.width(32)) x13 (.D(WriteData), .en(w13), .clk(clk), .Q(o13));  // open: clr
  Register #(.width(32)) x23 (.D(WriteData), .en(w23), .clk(clk), .Q(o23));  // open: clr
  Register #(.width(32)) x14 (.D(WriteData), .en(w14), .clk(clk), .Q(o14));  // open: clr
  Register #(.width(32)) x15 (.D(WriteData), .en(w15), .clk(clk), .Q(o15));  // open: clr
  Register #(.width(32)) x16 (.D(WriteData), .en(w16), .clk(clk), .Q(o16));  // open: clr
  Register #(.width(32)) x17 (.D(WriteData), .en(w17), .clk(clk), .Q(o17));  // open: clr
  Register #(.width(32)) x18 (.D(WriteData), .en(w18), .clk(clk), .Q(o18));  // open: clr
  Register #(.width(32)) x19 (.D(WriteData), .en(w19), .clk(clk), .Q(o19));  // open: clr
  Register #(.width(32)) x20 (.D(WriteData), .en(w20), .clk(clk), .Q(o20));  // open: clr
  Register #(.width(32)) x21 (.D(WriteData), .en(w21), .clk(clk), .Q(o21));  // open: clr
  Register #(.width(32)) x22 (.D(WriteData), .en(w22), .clk(clk), .Q(o22));  // open: clr
  Register #(.width(32)) x24 (.D(WriteData), .en(w24), .clk(clk), .Q(o24));  // open: clr
  Register #(.width(32)) x31 (.D(WriteData), .en(w31), .clk(clk), .Q(o31));  // open: clr
  Register #(.width(32)) x25 (.D(WriteData), .en(w25), .clk(clk), .Q(o25));  // open: clr
  Register #(.width(32)) x26 (.D(WriteData), .en(w26), .clk(clk), .Q(o26));  // open: clr
  Register #(.width(32)) x27 (.D(WriteData), .en(w27), .clk(clk), .Q(o27));  // open: clr
  Register #(.width(32)) x28 (.D(WriteData), .en(w28), .clk(clk), .Q(o28));  // open: clr
  Register #(.width(32)) x29 (.D(WriteData), .en(w29), .clk(clk), .Q(o29));  // open: clr
  Register #(.width(32)) x30 (.D(WriteData), .en(w30), .clk(clk), .Q(o30));  // open: clr

  // Other names for the same wires on the sheet: o1[31:0] = ra; o2[31:0] = sp; o5[31:0] = t0; o6[31:0] = t1;
  //   o7[31:0] = t2; o8[31:0] = s0; o9[31:0] = s1; o10[31:0] = a0

  // Notes on the sheet:
  //   INPUTS to your circuit
  //   DON'T CHANGE THE LOCATIONS OF THE INPUTS AND OUTPUTS!
  //   These are DEBUG/TEST outputs from your circuit.
  //   OUTPUTS from your circuit
endmodule
