// Logisim project sll.circ as structural Verilog: 1 circuit, main circuit main
module main (
  input  [31:0] in_1,
  input  [31:0] in_2,
  input  [31:0] in_3
);

  wire [31:0] s2, s4, s8, s16;

  Multiplexer #(.width(32)) multiplexer_1 (.in0(in_2), .in1({in_2[30:0], 1'b0}), .out(s2), .sel(in_3[0]));
  Multiplexer #(.width(32)) multiplexer_2 (.in0(s2), .in1({s2[29:0], 2'b00}), .out(s4), .sel(in_3[1]));
  Multiplexer #(.width(32)) multiplexer_3 (.in0(s4), .in1({s4[27:0], 4'b0000}), .out(s8), .sel(in_3[2]));
  Multiplexer #(.width(32)) multiplexer_4 (.in0(s8), .in1({s8[23:0], {8{1'b0}}}), .out(s16), .sel(in_3[3]));
  Multiplexer #(.width(32)) multiplexer_5 (.in0(s16), .in1({s16[15:0], {16{1'b0}}}), .out(in_1), .sel(in_3[4]));

  // Other names for the same wires on the sheet: s1[31:0] = in_2; s1o[31:1] = in_2[30:0]; s2o[31:2] = s2[29:0];
  //   s4o[31:4] = s4[27:0]; s8o[31:8] = s8[23:0]; s16o[31:16] = s16[15:0]
endmodule
